# Fritzing sketch hvacpcb (saved by Fritzing 0.9.3b)
circuit board: 5.92138cm x 6.01101cm
breadboards: 1

parts:
  D2 = LED - 3mm [color="Red (633nm)" package="3 mm [THT]"]
  R4 = Resistor [tolerance=±5% resistance=3.9k package=THT]
  R5 = Resistor [tolerance=±5% resistance=3.9k package=THT]
  R7 = Resistor [tolerance=±5% resistance=4.7k package=THT]
  JP4 = Header 4 [part_number=BME package=molex-1x4_lock]
  Q1 = MOSFET-NCHANNEL [package=to-92]
  R6 = Resistor [tolerance=±5% resistance=4.7k package=THT]
  Q2 = MOSFET-NCHANNEL [package=to-92]
  R1 = Resistor [tolerance=±5% resistance=1k package="1206 [SMD]"]
  R9 = Resistor [tolerance=±5% resistance=1k package=THT]
  U$1 = Header 4 [part_number=PCF8591 package=molex-1x4_lock]
  Sound1 = Header 2 [package=molex-1x2_lock]
  Sound2 = Header 2 [package=molex-1x2_lock]
  Moisture = Header 3 [package=molex-1x3_lock]
  Touch = Header 3 [package=molex-1x3_lock]
  Raspberry_Pi_3 = Raspberry Pi 3 [part_number=RPI-3-V1.2]

nets:
  N1: D2.cathode, Raspberry_Pi_3.GPIO17
  N2: D2.anode, R1.Pin_0, R9.Pin_0
  3V3: R4.Pin_0, R5.Pin_0, JP4.2, Q1.G, Q2.G, Moisture.2, Raspberry_Pi_3.3v3, Raspberry_Pi_3.3V3
  3.3V SCL: R4.Pin_1, JP4.4, Q2.S, Raspberry_Pi_3.GPIO3
  3.3V SDA: R5.Pin_1, JP4.3, Q1.S, Raspberry_Pi_3.GPIO2
  N3: R7.Pin_0, R6.Pin_0, U$1.1, Sound1.1, Sound2.1, Touch.1, Raspberry_Pi_3.5V
  5V SCL: R7.Pin_1, Q2.D, U$1.4, Touch.3
  N4: JP4.1, U$1.2, Sound1.2, Sound2.2, Moisture.1, Touch.2, Raspberry_Pi_3.GND
  5V SDA: Q1.D, R6.Pin_1, U$1.3
  N5: R1.Pin_1, R9.Pin_1, Raspberry_Pi_3.GPIO18
  N6: Moisture.3, Raspberry_Pi_3.GPIO24

notes:
  5V
  PCF
  Water Sens
  GND
  3.3V
  SDA
  SCL
  BCM24
  HVAC
  BME
  StudentSenseHatV06

custom parts:
  MOSFET-NCHANNEL: Generic NMOS footprint
